# Fritzing sketch dispenser_sketch (saved by Fritzing 0.9.3b)

parts:
  U1 = Power Outlet [chip_label=IC package="SIP (Single Inline) [THT]"]
  Sonoff_Dual_R1 = Sonoff Dual R2
  MOTOR2 = 28BYJ-48 Stepper Motor
  X2 = X113647 Stepper Driver Board [package=board]
  Power1 = PowerBRICK 12V
  U3 = NodeMCU V3.0
  MOTOR3 = 28BYJ-48 Stepper Motor

nets:
  N1: U1.hot2, Sonoff_Dual_R1.L_IN
  N2: U1.neutral2, Sonoff_Dual_R1.N1
  N3: Sonoff_Dual_R1.N3, Power1.GND
  N4: Sonoff_Dual_R1.L_Out_1, Power1.+Vin
  N5: MOTOR2.BLUE, X2.RED, MOTOR3.YELLOW
  N6: MOTOR2.PINK, X2.PINK, MOTOR3.PINK
  N7: MOTOR2.RED, X2.YELLOW, MOTOR3.RED
  N8: MOTOR2.ORANGE, X2.ORANGE, MOTOR3.ORANGE
  N9: MOTOR2.YELLOW, X2.BLUE, MOTOR3.BLUE
  N10: X2.IN1, U3.D0
  N11: X2.IN2, U3.D1
  N12: X2.IN3, U3.D2
  N13: X2.IN4, U3.D3
  GND: X2.GND, Power1.-Vout, U3.GND
  N14: X2.+V, Power1.+Vout, U3.Vin

notes:
  12V Converter

custom parts:
  Power Outlet: A standard power outlet. Silver screws are neutral, brass screws are hot. Green screw is ground.
  Sonoff Dual R2: Module Sonoff Dual R2 Wifi ESP32 avec 2 relais
  28BYJ-48 Stepper Motor: 28BYJ-48 gear-reduction stepper motor (small)
  X113647 Stepper Driver Board: A common stepper motor driver board based on ULN2003APG darlington array
  PowerBRICK 12V: PowerBRICKs are split-rail power supply modules that are intended to be used with a breadboard. These generate both a negative and positive voltage out of a single 5V USB voltage.
  NodeMCU V3.0: ESP8266 based NodeMCU
