# Fritzing sketch heater_sketch (saved by Fritzing 0.9.3b)

parts:
  U1 = Power Outlet [chip_label=IC package="SIP (Single Inline) [THT]"]
  Sonoff_Dual_R1 = Sonoff Dual R2
  Heating_Pad1 = SparkFun_Heating_Pad [part_number=COM-11288 package=5cmx10cm]

nets:
  N1: U1.hot2, Sonoff_Dual_R1.L_IN
  N2: U1.neutral2, Sonoff_Dual_R1.N1
  N3: Sonoff_Dual_R1.N3, Heating_Pad1.-
  N4: Sonoff_Dual_R1.L_Out_1, Heating_Pad1.+

custom parts:
  Power Outlet: A standard power outlet. Silver screws are neutral, brass screws are hot. Green screw is ground.
  Sonoff Dual R2: Module Sonoff Dual R2 Wifi ESP32 avec 2 relais
  SparkFun_Heating_Pad: Description: These DC powered heating pads are perfect for near-body heating applications. They get warm to the touch but not too hot. Simply apply 5VDC to the wire leads and within minutes, the pad will begin to warm up. These heating pads are constructed using a mesh of Polyester filament and Micro Metal Conductive Fiber folded into a protective Polyimide Film. The fact that these are low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
