# Fritzing sketch light_sketch (saved by Fritzing 0.9.3b)

parts:
  Sonoff_Dual_R1 = Sonoff Dual R2
  RGB_Strip_LED3 = RGB Strip LED
  U2 = Power Outlet [chip_label=IC package="SIP (Single Inline) [THT]"]
  Power1 = PowerBRICK 12V

nets:
  N1: Sonoff_Dual_R1.L_IN, U2.hot2
  N2: Sonoff_Dual_R1.N1, U2.neutral2
  N3: Sonoff_Dual_R1.N3, Power1.GND
  N4: Sonoff_Dual_R1.L_Out_1, Power1.+Vin
  N5: RGB_Strip_LED3.Common_Connect, Power1.+Vout
  N6: RGB_Strip_LED3.Green_Connect, RGB_Strip_LED3.Red_Connect, RGB_Strip_LED3.Blue_Connect, Power1.-Vout

notes:
  12V Converter

custom parts:
  Sonoff Dual R2: Module Sonoff Dual R2 Wifi ESP32 avec 2 relais
  RGB Strip LED: A tri-color Strip LED with red, green and blue. Based on LED SMD 5050 RGB Pin order: common cathode - green - red - blue
  Power Outlet: A standard power outlet. Silver screws are neutral, brass screws are hot. Green screw is ground.
  PowerBRICK 12V: PowerBRICKs are split-rail power supply modules that are intended to be used with a breadboard. These generate both a negative and positive voltage out of a single 5V USB voltage.
