# Fritzing sketch temperature_sketch (saved by Fritzing 0.9.3b)

parts:
  RHT2 = Humidity and Temperature Sensor RHT03 [part_number=DHT22]
  Sonoff_Dual_R1 = Sonoff Dual R2
  U1 = NodeMCU V3.0
  U2 = Power Outlet [chip_label=IC package="SIP (Single Inline) [THT]"]
  Power1 = PowerBRICK 12V

nets:
  VCC: RHT2.Vcc, U1.3V3
  N1: RHT2.Data-signal, U1.D0
  N2: RHT2.GND_2, U1.GND, Power1.-Vout
  N3: Sonoff_Dual_R1.L_IN, U2.hot2
  N4: Sonoff_Dual_R1.N1, U2.neutral2
  N5: Sonoff_Dual_R1.N3, Power1.GND
  N6: Sonoff_Dual_R1.L_Out_1, Power1.+Vin
  N7: U1.Vin, Power1.+Vout

notes:
  5V Converter

custom parts:
  Sonoff Dual R2: Module Sonoff Dual R2 Wifi ESP32 avec 2 relais
  NodeMCU V3.0: ESP8266 based NodeMCU
  Power Outlet: A standard power outlet. Silver screws are neutral, brass screws are hot. Green screw is ground.
  PowerBRICK 12V: PowerBRICKs are split-rail power supply modules that are intended to be used with a breadboard. These generate both a negative and positive voltage out of a single 5V USB voltage.
